# Fritzing sketch MusicalKeyboard (saved by Fritzing 0.6.3b)
breadboards: 1

parts:
  Arduino1 = Arduino  # not connected
  S1 = Pushbutton [package="[THT]"]
  S2 = Pushbutton [package="[THT]"]
  S3 = Pushbutton [package="[THT]"]
  S4 = Pushbutton [package="[THT]"]
  S5 = Pushbutton [package="[THT]"]
  S6 = Pushbutton [package="[THT]"]
  J1 = Piezo Speaker  # not connected
  R1 = Resistor [tolerance=±5% resistance=220 package=THT]
  R2 = Resistor [tolerance=±5% resistance=220 package=THT]
  R3 = Resistor [tolerance=±5% resistance=220 package=THT]  # not connected
  R4 = Resistor [tolerance=±5% resistance=220 package=THT]
  R5 = Resistor [tolerance=±5% resistance=220 package=THT]
  R6 = Resistor [tolerance=±5% resistance=220 package=THT]

nets:
  N1: S1.Pin_1, S1.Pin_2
  N2: S1.Pin_3, S1.Pin_4
  N3: S2.Pin_1, S2.Pin_2
  N4: S2.Pin_3, S2.Pin_4
  N5: S3.Pin_1, S3.Pin_2
  N6: S3.Pin_3, S3.Pin_4
  N7: S4.Pin_1, S4.Pin_2, S4.Pin_3, S4.Pin_4, R4.Pin_1
  N8: S5.Pin_1, S5.Pin_2
  N9: S5.Pin_3, S5.Pin_4
  N10: S6.Pin_1, S6.Pin_2, S6.Pin_3, S6.Pin_4, R6.Pin_1
  N11: R1.Pin_0, R2.Pin_0, R4.Pin_0, R5.Pin_0, R6.Pin_0
